# Fritzing sketch project (saved by Fritzing 0.9.5d)
breadboards: 2

parts:
  Part1 = Arduino Mega 2560 (Rev3)
  Part2 = KY-015 Temperature & Humidity Sensor Module [package="Breakout board"]
  ZS-042_RTC1 = ZS-042 RTC Module
  S1 = Pushbutton [package="[THT]"]
  R1 = Trimmer Potentiometer [maximum_resistance=10kΩ package=THT]
  LCD1 = LCD screen
  YwRobot_Power_Supply1 = YwRobot Breadboard Power Supply [part_number=545043]
  R2 = Trimmer Potentiometer [maximum_resistance=10kΩ package=THT]
  R3 = Resistor [tolerance=±5% resistance=220 package=THT]
  Water_Level_Sensor1 = Water Level Sensor [package=board]
  VCC1 = Battery block 9V  # not connected
  LED2 = LED - 5mm [color="Green (560nm)" package="5 mm [THT]"]
  LED3 = LED - 5mm [color="Blue (470nm)" package="5 mm [THT]"]
  LED4 = LED - 5mm [color="Yellow (592nm)" package="5 mm [THT]"]
  LED5 = LED - 5mm [color="Red (633nm)" package="5 mm [THT]"]
  M1 = Dagu DGServo 9g (Top view) [part_number=RS001B]
  M2 = DC Motor
  IC1 = L293D [package=THT]

nets:
  N1: Part1.A0, Water_Level_Sensor1.SIG
  N2: Part1.A1, R1.wiper
  N3: Part1.D21/SCL, ZS-042_RTC1.SCL
  N4: Part1.D20/SDA, ZS-042_RTC1.SDA
  N5: Part1.D19/RX1, Part2.S
  N6: Part1.D18/TX1, S1.Pin_3, S1.Pin_4
  N7: Part1.D12_PWM, LCD1.RS
  N8: Part1.D11_PWM, LCD1.E
  N9: Part1.D8_PWM, M1.pulse
  N10: Part1.D2_PWM, LCD1.DB7
  N11: Part1.D3_PWM, LCD1.DB6
  N12: Part1.D4_PWM, LCD1.DB5
  N13: Part1.D5_PWM, LCD1.DB4
  N14: Part1.D23, LED4.anode
  N15: Part1.D25, LED2.anode
  N16: Part1.D27, LED3.anode
  N17: Part1.D28, IC1.Enable_1
  N18: Part1.D29, LED5.anode
  VIN: Part2.Vin, R1.leg2, YwRobot_Power_Supply1.VCC#5, Water_Level_Sensor1.VCC, IC1.+V
  N19: Part2.-, S1.Pin_1, S1.Pin_2, R1.leg1, YwRobot_Power_Supply1.GND#11, Water_Level_Sensor1.GND, LED2.cathode, LED3.cathode, LED4.cathode, LED5.cathode, IC1.0V
  GND: ZS-042_RTC1.GND, LCD1.VSS, LCD1.R/W, LCD1.LED-, YwRobot_Power_Supply1.GND#13, R2.leg1
  VCC: ZS-042_RTC1.VCC, LCD1.VDD, YwRobot_Power_Supply1.VCC#9, R2.leg2, R3.Pin_0
  N20: LCD1.V0, R2.wiper
  N21: LCD1.LED+, R3.Pin_1
  N22: M2.pin_1, IC1.In_1
  N23: M2.pin_2, IC1.Out_1_(_Controlled_by_Enable_1_)

custom parts:
  KY-015 Temperature & Humidity Sensor Module: DH-11 temperature and humidity sensor in KEYES KY-015 module, provides a low-latency serial interface to measure humidity and temperature.
  YwRobot Breadboard Power Supply: The YwRobot Breadboard Power Supply (MB-V2) has two power rails; they can be 5V or 3V3. Power to the module can be provided through the female USB socket or through the A10 (female) 2.1mm power jack.
  Water Level Sensor: A water level sensor. This sensor operates at 3V to 5V. The Sig (signal) pin outputs an analogue signal that is in proportion to the amount of water in contact with the sensor.
